// Logisim project branch_comp.circ as structural Verilog: 1 circuit, main circuit branch_comp
module branch_comp (
  input  [31:0] rs1,
  input  [31:0] rs2,
  input  BrUn,
  output BrEq,
  output BrLt
);

  wire Signed_eq, Signed_lt, Unsigned_eq, Unsigned_lt;

  Comparator #(.mode("unsigned"), .width(32)) comparator_1 (
    .a(rs1), .b(rs2), .eq(Unsigned_eq), .lt(Unsigned_lt));  // open: gt
  Comparator #(.width(32)) comparator_2 (.a(rs1), .b(rs2), .eq(Signed_eq), .lt(Signed_lt));  // open: gt
  Multiplexer #(.enable("false")) multiplexer_1 (.in0(Unsigned_eq), .in1(Signed_eq), .out(BrEq), .sel(BrUn));
  Multiplexer #(.enable("false")) multiplexer_2 (.in0(Unsigned_lt), .in1(Signed_lt), .out(BrLt), .sel(BrUn));

  // Notes on the sheet:
  //   INPUTS to your circuit
  //   DON'T CHANGE THE LOCATIONS OF THE INPUTS AND OUTPUTS!
  //   OUTPUT from your circuit
endmodule
