// Logisim project control_logic.circ as structural Verilog: 1 circuit, main circuit control_logic
module control_logic (
  input  [31:0] inst,
  input  BrEq,
  input  BrLt,
  output PCSel,
  output RegWEn,
  output [2:0] ImmSel,
  output BrUn,
  output ASel,
  output BSel,
  output [3:0] ALUSel,
  output MemRW,
  output [1:0] WBSel,
  output CSRSel,
  output CSRWen
);

  wire and_1_out, and_2_out, and_3_out, and_4_out, and_5_out, and_6_out, and_7_out, and_8_out, and_9_out,
       and_10_out, and_11_out, and_12_out, and_13_out, and_14_out, and_15_out, and_16_out, and_17_out,
       and_18_out, and_19_out, and_20_out, and_21_out, and_22_out, and_23_out, and_24_out, and_25_out,
       and_26_out, and_27_out, comparator_2_eq, comparator_3_eq, comparator_4_eq, comparator_5_eq,
       comparator_6_eq, comparator_7_eq, comparator_8_eq, comparator_9_eq, comparator_10_eq,
       comparator_11_eq, comparator_12_eq, comparator_13_eq, comparator_14_eq, comparator_15_eq,
       comparator_16_eq, comparator_17_eq, comparator_18_eq, comparator_19_eq, comparator_20_eq,
       comparator_21_eq, comparator_22_eq, comparator_23_eq, comparator_24_eq, comparator_25_eq,
       comparator_26_eq, comparator_27_eq, comparator_28_eq, comparator_29_eq, comparator_30_eq,
       comparator_31_eq, comparator_32_eq, comparator_33_eq, comparator_34_eq, comparator_35_eq,
       comparator_36_eq, comparator_37_eq, comparator_38_eq, comparator_39_eq, comparator_40_eq,
       comparator_41_eq, comparator_42_eq, comparator_43_eq, comparator_44_eq, comparator_45_eq,
       comparator_46_eq, comparator_47_eq, comparator_48_eq, comparator_49_eq, comparator_50_eq,
       comparator_51_eq, comparator_52_eq, comparator_53_eq, comparator_54_eq, comparator_55_eq,
       comparator_56_eq, comparator_57_eq, comparator_58_eq, comparator_59_eq, comparator_60_eq,
       comparator_61_eq, comparator_62_eq, comparator_63_eq, comparator_64_eq, comparator_65_eq,
       comparator_66_eq, comparator_67_eq, comparator_69_eq, comparator_70_eq, comparator_71_eq,
       comparator_72_eq, comparator_73_eq, comparator_74_eq, comparator_75_eq, comparator_76_eq,
       comparator_77_eq, comparator_79_eq, comparator_81_eq, not_1_out, not_2_out, not_3_out, or_1_out,
       or_2_out;

  Comparator #(.width(7)) comparator_1 (.a(inst[6:0]), .b(7'b0110011), .eq(ASel));  // open: gt, lt
  Comparator #(.width(7)) comparator_2 (.a(inst[6:0]), .b(7'b0110011), .eq(comparator_2_eq));  // open: gt, lt
  Comparator #(.width(3)) comparator_3 (.a(inst[14:12]), .b(3'b000), .eq(comparator_3_eq));  // open: gt, lt
  Comparator #(.width(7)) comparator_4 (.a(inst[31:25]), .b({7{1'b0}}), .eq(comparator_4_eq));  // open: gt, lt
  Comparator #(.width(7)) comparator_5 (.a(inst[31:25]), .b(7'b0000001), .eq(comparator_5_eq));  // open: gt, lt
  Comparator #(.width(7)) comparator_6 (.a(inst[31:25]), .b(7'b0100000), .eq(comparator_6_eq));  // open: gt, lt
  Comparator #(.width(7)) comparator_7 (.a(inst[6:0]), .b(7'b0110011), .eq(comparator_7_eq));  // open: gt, lt
  Comparator #(.width(3)) comparator_8 (.a(inst[14:12]), .b(3'b001), .eq(comparator_8_eq));  // open: gt, lt
  Comparator #(.width(7)) comparator_9 (.a(inst[31:25]), .b({7{1'b0}}), .eq(comparator_9_eq));  // open: gt, lt
  Comparator #(.width(7)) comparator_10 (.a(inst[31:25]), .b(7'b0000001), .eq(comparator_10_eq));  // open: gt, lt
  Comparator #(.width(7)) comparator_11 (.a(inst[6:0]), .b(7'b0110011), .eq(comparator_11_eq));  // open: gt, lt
  Comparator #(.width(3)) comparator_12 (.a(inst[14:12]), .b(3'b010), .eq(comparator_12_eq));  // open: gt, lt
  Comparator #(.width(7)) comparator_13 (.a(inst[31:25]), .b({7{1'b0}}), .eq(comparator_13_eq));  // open: gt, lt
  Comparator #(.width(7)) comparator_14 (.a(inst[6:0]), .b(7'b0110011), .eq(comparator_14_eq));  // open: gt, lt
  Comparator #(.width(3)) comparator_15 (.a(inst[14:12]), .b(3'b011), .eq(comparator_15_eq));  // open: gt, lt
  Comparator #(.width(7)) comparator_16 (.a(inst[31:25]), .b(7'b0000001), .eq(comparator_16_eq));  // open: gt, lt
  Comparator #(.width(7)) comparator_17 (.a(inst[6:0]), .b(7'b0000011), .eq(comparator_17_eq));  // open: gt, lt
  Comparator #(.width(7)) comparator_18 (.a(inst[6:0]), .b(7'b0010011), .eq(comparator_18_eq));  // open: gt, lt
  Comparator #(.width(7)) comparator_19 (.a(inst[6:0]), .b(7'b0010011), .eq(comparator_19_eq));  // open: gt, lt
  Comparator #(.width(3)) comparator_20 (.a(inst[14:12]), .b(3'b000), .eq(comparator_20_eq));  // open: gt, lt
  Comparator #(.width(7)) comparator_21 (.a(inst[6:0]), .b(7'b0010011), .eq(comparator_21_eq));  // open: gt, lt
  Comparator #(.width(3)) comparator_22 (.a(inst[14:12]), .b(3'b001), .eq(comparator_22_eq));  // open: gt, lt
  Comparator #(.width(7)) comparator_23 (.a(inst[31:25]), .b({7{1'b0}}), .eq(comparator_23_eq));  // open: gt, lt
  Comparator #(.width(7)) comparator_24 (.a(inst[6:0]), .b(7'b0010011), .eq(comparator_24_eq));  // open: gt, lt
  Comparator #(.width(3)) comparator_25 (.a(inst[14:12]), .b(3'b010), .eq(comparator_25_eq));  // open: gt, lt
  Comparator #(.width(7)) comparator_26 (.a(inst[6:0]), .b(7'b0010011), .eq(comparator_26_eq));  // open: gt, lt
  Comparator #(.width(3)) comparator_27 (.a(inst[14:12]), .b(3'b100), .eq(comparator_27_eq));  // open: gt, lt
  Comparator #(.width(7)) comparator_28 (.a(inst[6:0]), .b(7'b0100011), .eq(comparator_28_eq));  // open: gt, lt
  Comparator #(.width(7)) comparator_29 (.a(inst[6:0]), .b(7'b0100011), .eq(comparator_29_eq));  // open: gt, lt
  Comparator #(.width(7)) comparator_30 (.a(inst[6:0]), .b(7'b0100011), .eq(comparator_30_eq));  // open: gt, lt
  Comparator #(.width(3)) comparator_31 (.a(inst[14:12]), .b(3'b010), .eq(comparator_31_eq));  // open: gt, lt
  and and_1 (and_1_out, comparator_2_eq, comparator_3_eq);
  and and_2 (and_2_out, comparator_7_eq, comparator_8_eq);
  and and_3 (and_3_out, comparator_11_eq, comparator_12_eq, comparator_13_eq);
  and and_4 (and_4_out, comparator_14_eq, comparator_15_eq, comparator_16_eq);
  or or_1 (or_1_out, comparator_17_eq, comparator_18_eq);
  and and_5 (and_5_out, comparator_19_eq, comparator_20_eq);
  and and_6 (and_6_out, comparator_21_eq, comparator_22_eq, comparator_23_eq);
  and and_7 (and_7_out, comparator_24_eq, comparator_25_eq);
  and and_8 (and_8_out, comparator_26_eq, comparator_27_eq);
  Multiplexer #(.enable("false"), .width(3)) multiplexer_1 (
    .in0(3'b000), .in1(3'b001), .out(ImmSel), .sel(comparator_28_eq));
  Multiplexer #(.enable("false")) multiplexer_2 (.in0(1'b0), .in1(1'b1), .out(MemRW), .sel(comparator_29_eq));
  and and_9 (and_9_out, comparator_30_eq, comparator_31_eq);
  and and_10 (and_10_out, and_2_out, comparator_9_eq);
  and and_11 (and_11_out, and_2_out, comparator_10_eq);
  Multiplexer #(.enable("false")) multiplexer_3 (.in0(1'b0), .in1(1'b1), .out(ASel), .sel(or_1_out));
  Multiplexer #(.enable("false"), .width(4)) multiplexer_4 (
    .in0(4'b0000), .in1(4'b0000), .out(ALUSel), .sel(and_5_out));
  Multiplexer #(.enable("false"), .width(4)) multiplexer_5 (
    .in0(4'b0000), .in1(4'b0110), .out(ALUSel), .sel(and_6_out));
  Multiplexer #(.enable("false"), .width(4)) multiplexer_6 (
    .in0(4'b0000), .in1(4'b0111), .out(ALUSel), .sel(and_7_out));
  Multiplexer #(.enable("false"), .width(4)) multiplexer_7 (
    .in0(4'b0000), .in1(4'b0011), .out(ALUSel), .sel(and_8_out));
  Multiplexer #(.enable("false")) multiplexer_8 (.in0(1'b0), .in1(1'b1), .out(ASel), .sel(and_9_out));
  Comparator #(.width(7)) comparator_32 (.a(inst[6:0]), .b(7'b0110011), .eq(comparator_32_eq));  // open: gt, lt
  and and_12 (and_12_out, and_1_out, comparator_4_eq);
  and and_13 (and_13_out, and_1_out, comparator_5_eq);
  and and_14 (and_14_out, and_1_out, comparator_6_eq);
  Multiplexer #(.enable("false"), .width(2)) multiplexer_9 (
    .in0(2'b00), .in1(2'b01), .out(WBSel), .sel(comparator_32_eq));
  Multiplexer #(.enable("false"), .width(4)) multiplexer_10 (
    .in0(4'b0000), .in1(4'b0000), .out(ALUSel), .sel(and_12_out));
  Multiplexer #(.enable("false"), .width(4)) multiplexer_11 (
    .in0(4'b0000), .in1(4'b1010), .out(ALUSel), .sel(and_13_out));
  Multiplexer #(.enable("false"), .width(4)) multiplexer_12 (
    .in0(4'b0000), .in1(4'b1100), .out(ALUSel), .sel(and_14_out));
  Multiplexer #(.enable("false"), .width(4)) multiplexer_13 (
    .in0(4'b0000), .in1(4'b0110), .out(ALUSel), .sel(and_10_out));
  Multiplexer #(.enable("false"), .width(4)) multiplexer_14 (
    .in0(4'b0000), .in1(4'b1110), .out(ALUSel), .sel(and_11_out));
  Multiplexer #(.enable("false"), .width(4)) multiplexer_15 (
    .in0(4'b0000), .in1(4'b0111), .out(ALUSel), .sel(and_3_out));
  Multiplexer #(.enable("false"), .width(4)) multiplexer_16 (
    .in0(4'b0000), .in1(4'b1011), .out(ALUSel), .sel(and_4_out));
  Comparator #(.width(7)) comparator_33 (.a(inst[6:0]), .b(7'b0010011), .eq(comparator_33_eq));  // open: gt, lt
  Comparator #(.width(7)) comparator_34 (.a(inst[6:0]), .b(7'b0010011), .eq(comparator_34_eq));  // open: gt, lt
  Comparator #(.width(3)) comparator_35 (.a(inst[14:12]), .b(3'b101), .eq(comparator_35_eq));  // open: gt, lt
  Comparator #(.width(7)) comparator_36 (.a(inst[31:25]), .b({7{1'b0}}), .eq(comparator_36_eq));  // open: gt, lt
  Comparator #(.width(7)) comparator_37 (.a(inst[6:0]), .b(7'b0010011), .eq(comparator_37_eq));  // open: gt, lt
  Comparator #(.width(3)) comparator_38 (.a(inst[14:12]), .b(3'b101), .eq(comparator_38_eq));  // open: gt, lt
  Comparator #(.width(7)) comparator_39 (.a(inst[31:25]), .b(7'b0100000), .eq(comparator_39_eq));  // open: gt, lt
  Comparator #(.width(7)) comparator_40 (.a(inst[6:0]), .b(7'b0010011), .eq(comparator_40_eq));  // open: gt, lt
  Comparator #(.width(3)) comparator_41 (.a(inst[14:12]), .b(3'b110), .eq(comparator_41_eq));  // open: gt, lt
  Comparator #(.width(7)) comparator_42 (.a(inst[6:0]), .b(7'b0010011), .eq(comparator_42_eq));  // open: gt, lt
  Comparator #(.width(3)) comparator_43 (.a(inst[14:12]), .b(3'b111), .eq(comparator_43_eq));  // open: gt, lt
  Multiplexer #(.enable("false"), .width(2)) multiplexer_17 (
    .in0(2'b00), .in1(2'b01), .out(WBSel), .sel(comparator_33_eq));
  and and_15 (and_15_out, comparator_34_eq, comparator_35_eq, comparator_36_eq);
  and and_16 (and_16_out, comparator_37_eq, comparator_38_eq, comparator_39_eq);
  and and_17 (and_17_out, comparator_40_eq, comparator_41_eq);
  and and_18 (and_18_out, comparator_42_eq, comparator_43_eq);
  Comparator #(.width(7)) comparator_44 (.a(inst[6:0]), .b(7'b0110011), .eq(comparator_44_eq));  // open: gt, lt
  Comparator #(.width(3)) comparator_45 (.a(inst[14:12]), .b(3'b101), .eq(comparator_45_eq));  // open: gt, lt
  Comparator #(.width(7)) comparator_46 (.a(inst[31:25]), .b(7'b0000001), .eq(comparator_46_eq));  // open: gt, lt
  Comparator #(.width(7)) comparator_47 (.a(inst[31:25]), .b({7{1'b0}}), .eq(comparator_47_eq));  // open: gt, lt
  Comparator #(.width(7)) comparator_48 (.a(inst[31:25]), .b(7'b0100000), .eq(comparator_48_eq));  // open: gt, lt
  Comparator #(.width(7)) comparator_49 (.a(inst[6:0]), .b(7'b0110011), .eq(comparator_49_eq));  // open: gt, lt
  Comparator #(.width(3)) comparator_50 (.a(inst[14:12]), .b(3'b111), .eq(comparator_50_eq));  // open: gt, lt
  Comparator #(.width(7)) comparator_51 (.a(inst[31:25]), .b({7{1'b0}}), .eq(comparator_51_eq));  // open: gt, lt
  Comparator #(.width(7)) comparator_52 (.a(inst[31:25]), .b(7'b0000001), .eq(comparator_52_eq));  // open: gt, lt
  Comparator #(.width(7)) comparator_53 (.a(inst[6:0]), .b(7'b0110011), .eq(comparator_53_eq));  // open: gt, lt
  Comparator #(.width(3)) comparator_54 (.a(inst[14:12]), .b(3'b110), .eq(comparator_54_eq));  // open: gt, lt
  Comparator #(.width(7)) comparator_55 (.a(inst[31:25]), .b({7{1'b0}}), .eq(comparator_55_eq));  // open: gt, lt
  Comparator #(.width(7)) comparator_56 (.a(inst[6:0]), .b(7'b0110011), .eq(comparator_56_eq));  // open: gt, lt
  Comparator #(.width(3)) comparator_57 (.a(inst[14:12]), .b(3'b100), .eq(comparator_57_eq));  // open: gt, lt
  Comparator #(.width(7)) comparator_58 (.a(inst[31:25]), .b({7{1'b0}}), .eq(comparator_58_eq));  // open: gt, lt
  Multiplexer #(.enable("false"), .width(4)) multiplexer_18 (
    .in0(4'b0000), .in1(4'b0100), .out(ALUSel), .sel(and_15_out));
  Multiplexer #(.enable("false"), .width(4)) multiplexer_19 (
    .in0(4'b0000), .in1(4'b0101), .out(ALUSel), .sel(and_16_out));
  Multiplexer #(.enable("false"), .width(4)) multiplexer_20 (
    .in0(4'b0000), .in1(4'b0010), .out(ALUSel), .sel(and_17_out));
  Multiplexer #(.enable("false"), .width(4)) multiplexer_21 (
    .in0(4'b0000), .in1(4'b0010), .out(ALUSel), .sel(and_18_out));
  and and_19 (and_19_out, comparator_44_eq, comparator_45_eq);
  and and_20 (and_20_out, comparator_49_eq, comparator_50_eq);
  and and_21 (and_21_out, comparator_53_eq, comparator_54_eq, comparator_55_eq);
  and and_22 (and_22_out, comparator_56_eq, comparator_57_eq, comparator_58_eq);
  and and_23 (and_23_out, and_19_out, comparator_46_eq);
  and and_24 (and_24_out, and_19_out, comparator_47_eq);
  and and_25 (and_25_out, and_19_out, comparator_48_eq);
  and and_26 (and_26_out, and_20_out, comparator_51_eq);
  and and_27 (and_27_out, and_20_out, comparator_52_eq);
  Multiplexer #(.enable("false"), .width(4)) multiplexer_22 (
    .in0(4'b0000), .in1(4'b1000), .out(ALUSel), .sel(and_23_out));
  Multiplexer #(.enable("false"), .width(4)) multiplexer_23 (
    .in0(4'b0000), .in1(4'b0100), .out(ALUSel), .sel(and_24_out));
  Multiplexer #(.enable("false"), .width(4)) multiplexer_24 (
    .in0(4'b0000), .in1(4'b0101), .out(ALUSel), .sel(and_25_out));
  Multiplexer #(.enable("false"), .width(4)) multiplexer_25 (
    .in0(4'b0000), .in1(4'b0001), .out(ALUSel), .sel(and_26_out));
  Multiplexer #(.enable("false"), .width(4)) multiplexer_26 (
    .in0(4'b0000), .in1(4'b1001), .out(ALUSel), .sel(and_27_out));
  Multiplexer #(.enable("false"), .width(4)) multiplexer_27 (
    .in0(4'b0000), .in1(4'b0010), .out(ALUSel), .sel(and_21_out));
  Multiplexer #(.enable("false"), .width(4)) multiplexer_28 (
    .in0(4'b0000), .in1(4'b0011), .out(ALUSel), .sel(and_22_out));
  Comparator #(.width(7)) comparator_59 (.a(inst[6:0]), .b(7'b1100011), .eq(comparator_59_eq));  // open: gt, lt
  Comparator #(.width(7)) comparator_60 (.a(inst[6:0]), .b(7'b1100011), .eq(comparator_60_eq));  // open: gt, lt
  Comparator #(.width(7)) comparator_61 (.a(inst[6:0]), .b(7'b1100011), .eq(comparator_61_eq));  // open: gt, lt
  Comparator #(.width(3)) comparator_62 (.a(inst[14:12]), .b(3'b100), .eq(comparator_62_eq));  // open: gt, lt
  Comparator #(.width(3)) comparator_63 (.a(inst[14:12]), .b(3'b101), .eq(comparator_63_eq));  // open: gt, lt
  Comparator #(.width(7)) comparator_64 (.a(inst[6:0]), .b(7'b1100011), .eq(comparator_64_eq));  // open: gt, lt
  Comparator #(.width(3)) comparator_65 (.a(inst[14:12]), .b(3'b000), .eq(comparator_65_eq));  // open: gt, lt
  Comparator #(.width(7)) comparator_66 (.a(inst[6:0]), .b(7'b1100011), .eq(comparator_66_eq));  // open: gt, lt
  Comparator #(.width(3)) comparator_67 (.a(inst[14:12]), .b(3'b001), .eq(comparator_67_eq));  // open: gt, lt
  not not_1 (not_1_out, BrEq);
  Comparator #(.width(7)) comparator_68 (.a(inst[6:0]), .b(7'b0010111), .eq(ASel));  // open: gt, lt
  Comparator #(.width(7)) comparator_69 (.a(inst[6:0]), .b(7'b0010111), .eq(comparator_69_eq));  // open: gt, lt
  Multiplexer #(.enable("false"), .width(3)) multiplexer_29 (
    .in0(3'b000), .in1(3'b010), .out(ImmSel), .sel(comparator_59_eq));
  Multiplexer #(.enable("false")) multiplexer_30 (.in0(1'b0), .in1(1'b1), .out(ASel), .sel(comparator_60_eq));
  and and_28 (ASel, comparator_64_eq, comparator_65_eq, BrEq);
  and and_29 (ASel, comparator_66_eq, comparator_67_eq, not_1_out);
  Multiplexer #(.enable("false"), .width(3)) multiplexer_31 (.in0(3'b000), .in1(3'b011), .out(ImmSel), .sel(ASel));
  Multiplexer #(.enable("false"), .width(2)) multiplexer_32 (
    .in0(2'b00), .in1(2'b01), .out(WBSel), .sel(comparator_69_eq));
  or or_2 (or_2_out, comparator_62_eq, comparator_63_eq);
  and and_30 (BrUn, comparator_61_eq, or_2_out);
  not not_2 (not_2_out, BrLt);
  not not_3 (not_3_out, BrLt);
  Comparator #(.width(7)) comparator_70 (.a(inst[6:0]), .b(7'b1100011), .eq(comparator_70_eq));  // open: gt, lt
  Comparator #(.width(3)) comparator_71 (.a(inst[14:12]), .b(3'b100), .eq(comparator_71_eq));  // open: gt, lt
  Comparator #(.width(7)) comparator_72 (.a(inst[6:0]), .b(7'b1100011), .eq(comparator_72_eq));  // open: gt, lt
  Comparator #(.width(3)) comparator_73 (.a(inst[14:12]), .b(3'b101), .eq(comparator_73_eq));  // open: gt, lt
  Comparator #(.width(7)) comparator_74 (.a(inst[6:0]), .b(7'b1100011), .eq(comparator_74_eq));  // open: gt, lt
  Comparator #(.width(3)) comparator_75 (.a(inst[14:12]), .b(3'b110), .eq(comparator_75_eq));  // open: gt, lt
  Comparator #(.width(7)) comparator_76 (.a(inst[6:0]), .b(7'b1100011), .eq(comparator_76_eq));  // open: gt, lt
  Comparator #(.width(3)) comparator_77 (.a(inst[14:12]), .b(3'b111), .eq(comparator_77_eq));  // open: gt, lt
  Comparator #(.width(7)) comparator_78 (.a(inst[6:0]), .b(7'b1101111), .eq(ASel));  // open: gt, lt
  Comparator #(.width(7)) comparator_79 (.a(inst[6:0]), .b(7'b1101111), .eq(comparator_79_eq));  // open: gt, lt
  Comparator #(.width(7)) comparator_80 (.a(inst[6:0]), .b(7'b1100111), .eq(ASel));  // open: gt, lt
  Comparator #(.width(7)) comparator_81 (.a(inst[6:0]), .b(7'b1100111), .eq(comparator_81_eq));  // open: gt, lt
  and and_31 (ASel, comparator_70_eq, comparator_71_eq, BrLt);
  and and_32 (ASel, comparator_72_eq, comparator_73_eq, not_2_out);
  and and_33 (ASel, comparator_74_eq, comparator_75_eq, BrLt);
  and and_34 (ASel, comparator_76_eq, comparator_77_eq, not_3_out);
  Multiplexer #(.enable("false"), .width(3)) multiplexer_33 (.in0(3'b000), .in1(3'b100), .out(ImmSel), .sel(ASel));
  Multiplexer #(.enable("false"), .width(2)) multiplexer_34 (
    .in0(2'b00), .in1(2'b10), .out(WBSel), .sel(comparator_79_eq));
  Multiplexer #(.enable("false"), .width(2)) multiplexer_35 (
    .in0(2'b00), .in1(2'b10), .out(WBSel), .sel(comparator_81_eq));

  assign BSel = ASel;
  assign PCSel = ASel;
  assign RegWEn = ASel;

  // Other names for the same wires on the sheet: opcode[6:0] = inst[6:0]; rd[4:0] = inst[11:7];
  //   func3[2:0] = inst[14:12]; rs1[4:0] = inst[19:15]; rs2[4:0] = inst[24:20]; func7[6:0] = inst[31:25]

  // Notes on the sheet:
  //   INPUTS to your circuit
  //   I-instruction
  //   DON'T CHANGE THE LOCATIONS OF THE INPUTS AND OUTPUTS!
  //   OUTPUT from your circuit
  //   R-isntruction
  //   Addi operation
  //   Slli operation
  //   Slti operation
  //   Xori operation
  //   Add operation
  //   Mul operation
  //   Sub operation
  //   Sll operation
  //   Mulh operation
  //   Slt operation
  //   Mulhu operation
  //   Srli operation
  //   Srli operation
  //   Ori operation
  //   Andi operation
  //   Divu operation
  //   Srl operation
  //   Sra operation
  //   And operation
  //   Remu operation
  //   Or operation
  //   Xor operation
  //   SB-instruction
  //   UJ-instruction
  //   jalr operation
endmodule
