// Logisim project cpu.circ as structural Verilog: 1 circuit, main circuit cpu
module cpu (
  input  clk,
  input  [31:0] INSTRUCTION,
  input  [31:0] READ_DATA,
  output [31:0] WRITE_ADDRESS,
  output [31:0] PROGRAM_COUNTER,
  output [31:0] ra,
  output [31:0] sp,
  output [31:0] t0,
  output [31:0] t1,
  output [31:0] t2,
  output [31:0] s0,
  output [31:0] s1,
  output [31:0] a0,
  output [31:0] tohost,
  output [3:0] WRITE_ENABLE,
  output [31:0] WRITE_DATA
);

  wire ASel, BrEq, BrLt, BrUn, BSel, comparator_1_eq, MemRW, PCSel, RegWEn;
  wire [1:0] WBSel;
  wire [2:0] immSel;
  wire [3:0] ALUSel;
  wire [31:0] adder_1_out, adder_2_out, ALU_rsc_1, ALU_rsc_2, imm, INSTRUCTION2, multiplexer_1_out,
       multiplexer_2_out, PROGRAM_COUNTER2, read_data_1, WRITE_BACK;

  Adder #(.width(32)) adder_1 (.a(PROGRAM_COUNTER), .b(32'h4), .out(adder_1_out));  // open: cin, cout
  Multiplexer #(.enable("false"), .width(32)) multiplexer_1 (
    .in0(adder_1_out), .in1(WRITE_ADDRESS), .out(multiplexer_1_out), .sel(PCSel));
  Multiplexer #(.enable("false"), .width(32)) multiplexer_2 (
    .in0(INSTRUCTION), .in1(32'h13), .out(multiplexer_2_out), .sel(PCSel));
  Register #(.width(32)) PC (.D(multiplexer_1_out), .clk(clk), .Q(PROGRAM_COUNTER));  // open: en, clr
  Register #(.width(32)) register_1 (.D(multiplexer_2_out), .clk(clk), .Q(INSTRUCTION2));  // open: en, clr
  Register #(.width(32)) register_2 (.D(PROGRAM_COUNTER), .clk(clk), .Q(PROGRAM_COUNTER2));  // open: en, clr
  control_logic control_logic_1 (
    .PCSel(PCSel), .RegWEn(RegWEn), .ImmSel(immSel), .BrUn(BrUn), .ASel(ASel), .BSel(BSel), .ALUSel(ALUSel),
    .MemRW(MemRW), .WBSel(WBSel), .inst(INSTRUCTION2), .BrEq(BrEq), .BrLt(BrLt));  // open: CSRWen, CSRSel
  Adder #(.width(32)) adder_2 (.a(PROGRAM_COUNTER2), .b(32'h4), .out(adder_2_out));  // open: cin, cout
  imm_gen imm_gen_1 (.inst(INSTRUCTION2), .ImmSel(immSel), .imm(imm));
  Multiplexer #(.enable("false"), .select(2), .width(32)) multiplexer_3 (
    .in0(READ_DATA), .in1(WRITE_ADDRESS), .in2(adder_2_out), .out(WRITE_BACK), .sel(WBSel));  // open: in3
  branch_comp branch_comp_1 (.rs1(read_data_1), .rs2(WRITE_DATA), .BrUn(BrUn), .BrEq(BrEq), .BrLt(BrLt));
  regfile regfile_1 (
    .rs1(INSTRUCTION2[19:15]), .rs2(INSTRUCTION2[24:20]), .rd(INSTRUCTION2[11:7]), .Write_Data(WRITE_BACK),
    .RegWEn(RegWEn), .clk(clk), .ra(ra), .sp(sp), .t0(t0), .t1(t1), .t2(t2), .s0(s0), .s1(s1), .a0(a0),
    .Read_Data_1(read_data_1), .Read_Data_2(WRITE_DATA));
  Comparator #(.width(1)) comparator_1 (.a(MemRW), .b(1'b1), .eq(comparator_1_eq));  // open: gt, lt
  Multiplexer #(.enable("false"), .width(4)) multiplexer_4 (
    .in0(4'b0000), .in1(4'b1111), .out(WRITE_ENABLE), .sel(comparator_1_eq));
  Multiplexer #(.enable("false"), .width(32)) multiplexer_5 (
    .in0(read_data_1), .in1(PROGRAM_COUNTER2), .out(ALU_rsc_1), .sel(ASel));
  Multiplexer #(.enable("false"), .width(32)) multiplexer_6 (.in0(WRITE_DATA), .in1(imm), .out(ALU_rsc_2), .sel(BSel));
  alu alu_1 (.Result(WRITE_ADDRESS), .A(ALU_rsc_1), .B(ALU_rsc_2), .ALUSel(ALUSel));

  // Other names for the same wires on the sheet: ALU_result[31:0] = WRITE_ADDRESS; rd[4:0] = INSTRUCTION2[11:7];
  //   rs1[4:0] = INSTRUCTION2[19:15]; rs2[4:0] = INSTRUCTION2[24:20]; read_data_2[31:0] = WRITE_DATA

  // Notes on the sheet:
  //   Output to IMEM
  //   IMEM (do **NOT** move this)
  //   Inputs from IMEM
  //   It is OK to move the PC, RegFile, ALU, MEM, Branch Comp, Imm Gen, and Control Logic to wherever is most convenient for you when constructing your CPU, and to delete this text
  //   Inputs/Outputs for testing. Do **NOT** move these.
  //   Outputs To DMEM
  //   DMEM (do **NOT** move this)
  //   Inputs From DMEM
endmodule
